# Fritzing sketch 01-arcade-system (saved by Fritzing 1.0.1)

parts:
  Pi = Raspberry Pi / kiosk
  Due = Arduino Due
  FPGA = Digilent Nexys Video
  Player_1 = Player controls
  Player_2 = Player controls
  HDMI_switch = HDMI switch
  Monitor = Monitor
  Speakers = Powered speakers
  Trackball = 3 inch USB trackball
  LED_buffer = LED interface / sheet 03
  Pixels = 3-4 SK6812 RGB pixels
  Switch_interface = HDMI status / sheet 03
  Silver_button = Silver HDMI button
  Read_me = Power and configuration  # not connected

nets:
  N1: Pi.USB_host_->_Due_Native, Due.Native_USB_/_HID
  N2: Pi.USB_host_->_FPGA_PROG, FPGA.PROG_micro-USB_/_JTAG
  N3: Pi.HDMI_output, HDMI_switch.Input_1_/_Pi
  N4: Due.P1_/_8_inputs_+_GND, Player_1.8_NO_contacts_+_common_GND
  N5: Due.P2_/_8_inputs_+_GND, Player_2.8_NO_contacts_+_common_GND
  N6: Due.P1_NES_/_D2_D3_D4, FPGA.JA1_/_JA2_/_JA3
  N7: Due.P2_NES_/_D5_D6_D7, FPGA.JA7_/_JA8_/_JA9
  N8: Due.Status_/_D8_GND, Switch_interface.Due_D8_/_GND
  N9: FPGA.HDMI_OUT, HDMI_switch.Input_2_/_FPGA
  N10: FPGA.Green_LINE_OUT, Speakers.3.5_mm_stereo_input
  N11: FPGA.J15_USB_HOST, Trackball.USB_cable_/_mouse
  N12: FPGA.JA4_/_LED_data, LED_buffer.JA4_/_3.3_V_data
  N13: FPGA.JA5_+_JA11_/_GND, LED_buffer.GND
  N14: HDMI_switch.Status_5_V_+_GND, Switch_interface.STATUS_5V_/_GND
  N15: HDMI_switch.Silver_button_/_NO_+_COM, Silver_button.NO_+_COM_/_switch_only
  N16: HDMI_switch.HDMI_to_monitor, Monitor.HDMI_input
  N17: LED_buffer.5_V_+_data_+_GND, Pixels.5_V_/_DIN_/_GND

custom parts:
  Raspberry Pi / kiosk: Logical wiring symbol. Connector labels identify real board pins or complete cables. Not a physical board footprint. PCB fabrication is not supported by this documentation part.
  Arduino Due: Logical wiring symbol. Connector labels identify real board pins or complete cables. Not a physical board footprint. PCB fabrication is not supported by this documentation part.
  Digilent Nexys Video: Logical wiring symbol. Connector labels identify real board pins or complete cables. Not a physical board footprint. PCB fabrication is not supported by this documentation part.
  Player controls: Logical wiring symbol. Connector labels identify real board pins or complete cables. Not a physical board footprint. PCB fabrication is not supported by this documentation part.
  HDMI switch: Logical wiring symbol. Connector labels identify real board pins or complete cables. Not a physical board footprint. PCB fabrication is not supported by this documentation part.
  Monitor: Logical wiring symbol. Connector labels identify real board pins or complete cables. Not a physical board footprint. PCB fabrication is not supported by this documentation part.
  Powered speakers: Logical wiring symbol. Connector labels identify real board pins or complete cables. Not a physical board footprint. PCB fabrication is not supported by this documentation part.
  3 inch USB trackball: Logical wiring symbol. Connector labels identify real board pins or complete cables. Not a physical board footprint. PCB fabrication is not supported by this documentation part.
  LED interface / sheet 03: Logical wiring symbol. Connector labels identify real board pins or complete cables. Not a physical board footprint. PCB fabrication is not supported by this documentation part.
  3-4 SK6812 RGB pixels: Logical wiring symbol. Connector labels identify real board pins or complete cables. Not a physical board footprint. PCB fabrication is not supported by this documentation part.
  HDMI status / sheet 03: Logical wiring symbol. Connector labels identify real board pins or complete cables. Not a physical board footprint. PCB fabrication is not supported by this documentation part.
  Silver HDMI button: Logical wiring symbol. Connector labels identify real board pins or complete cables. Not a physical board footprint. PCB fabrication is not supported by this documentation part.
  Power and configuration: Logical wiring symbol. Connector labels identify real board pins or complete cables. Not a physical board footprint. PCB fabrication is not supported by this documentation part.
