# Fritzing sketch 02-controls-and-ja (saved by Fritzing 1.0.1)

parts:
  Due = Arduino Due / control pins
  JA = Nexys Video / JA
  P1_joystick = 4-way joystick contacts
  P1_START = NO pushbutton
  P1_SELECT = NO pushbutton
  P1_A = NO pushbutton
  P1_B = NO pushbutton
  P2_joystick = 4-way joystick contacts
  P2_START = NO pushbutton
  P2_SELECT = NO pushbutton
  P2_A = NO pushbutton
  P2_B = NO pushbutton
  R6_10_kohm = 10 kohm NES pull-up
  R7_10_kohm = 10 kohm NES pull-up
  JA_orientation = JA - front / mating face, as in your screenshot  # not connected
  NES_behavior = Firmware contract  # not connected
  Contact_note = Controls and ground  # not connected

nets:
  N1: Due.D22_/_P1_A, P1_A.NO_/_signal
  N2: Due.D23_/_P1_B, P1_B.NO_/_signal
  N3: Due.D24_/_P1_SELECT, P1_SELECT.NO_/_signal
  N4: Due.D25_/_P1_START, P1_START.NO_/_signal
  N5: Due.D26_/_P1_UP, P1_joystick.UP_/_NO
  N6: Due.D27_/_P1_DOWN, P1_joystick.DOWN_/_NO
  N7: Due.D28_/_P1_LEFT, P1_joystick.LEFT_/_NO
  N8: Due.D29_/_P1_RIGHT, P1_joystick.RIGHT_/_NO
  N9: Due.D30_/_P2_A, P2_A.NO_/_signal
  N10: Due.D31_/_P2_B, P2_B.NO_/_signal
  N11: Due.D32_/_P2_SELECT, P2_SELECT.NO_/_signal
  N12: Due.D33_/_P2_START, P2_START.NO_/_signal
  N13: Due.D34_/_P2_UP, P2_joystick.UP_/_NO
  N14: Due.D35_/_P2_DOWN, P2_joystick.DOWN_/_NO
  N15: Due.D36_/_P2_LEFT, P2_joystick.LEFT_/_NO
  N16: Due.D37_/_P2_RIGHT, P2_joystick.RIGHT_/_NO
  N17: Due.GND_/_switch_commons, Due.GND_/_FPGA_reference, JA.JA5_/_GND, JA.JA11_/_GND, P1_joystick.All_COM_terminals_/_GND, P1_START.COM_/_GND, P1_SELECT.COM_/_GND, P1_A.COM_/_GND, P1_B.COM_/_GND, P2_joystick.All_COM_terminals_/_GND, P2_START.COM_/_GND, P2_SELECT.COM_/_GND, P2_A.COM_/_GND, P2_B.COM_/_GND
  N18: Due.D2_/_P1_latch_IN, JA.JA1_/_P1_LATCH_->
  N19: Due.D3_/_P1_clock_IN, JA.JA2_/_P1_CLOCK_->
  N20: Due.D4_/_P1_data_OUT, JA.JA3_/_P1_DATA_<-, R6_10_kohm.2
  N21: Due.D5_/_P2_latch_IN, JA.JA7_/_P2_LATCH_->
  N22: Due.D6_/_P2_clock_IN, JA.JA8_/_P2_CLOCK_->
  N23: Due.D7_/_P2_data_OUT, JA.JA9_/_P2_DATA_<-, R7_10_kohm.2
  N24: JA.JA6_/_3.3_V_/_R6_R7, R6_10_kohm.1, R7_10_kohm.1

custom parts:
  Arduino Due / control pins: Logical wiring symbol. Connector labels identify real board pins or complete cables. Not a physical board footprint. PCB fabrication is not supported by this documentation part.
  Nexys Video / JA: Logical wiring symbol. Connector labels identify real board pins or complete cables. Not a physical board footprint. PCB fabrication is not supported by this documentation part.
  4-way joystick contacts: Logical wiring symbol. Connector labels identify real board pins or complete cables. Not a physical board footprint. PCB fabrication is not supported by this documentation part.
  NO pushbutton: Logical wiring symbol. Connector labels identify real board pins or complete cables. Not a physical board footprint. PCB fabrication is not supported by this documentation part.
  10 kohm NES pull-up: Logical wiring symbol. Connector labels identify real board pins or complete cables. Not a physical board footprint. PCB fabrication is not supported by this documentation part.
  JA - front / mating face, as in your screenshot: Logical wiring symbol. Connector labels identify real board pins or complete cables. Not a physical board footprint. PCB fabrication is not supported by this documentation part.
  Firmware contract: Logical wiring symbol. Connector labels identify real board pins or complete cables. Not a physical board footprint. PCB fabrication is not supported by this documentation part.
  Controls and ground: Logical wiring symbol. Connector labels identify real board pins or complete cables. Not a physical board footprint. PCB fabrication is not supported by this documentation part.
