# Fritzing sketch 03-led-and-hdmi-interfaces (saved by Fritzing 1.0.1)

parts:
  JA = Nexys Video / JA
  LED_power = Regulated LED supply
  U1 = U1 / SN74HCT245N / 5 V
  R1_330_ohm = Resistor
  LED1 = SK6812 RGB pixel
  LED2 = SK6812 RGB pixel
  LED3 = SK6812 RGB pixel
  LED4_optional = SK6812 RGB pixel
  C1_100_nF = Capacitor
  C3_1000_uF_10_V = Capacitor
  R4_10_kohm = Resistor
  LED_notes = LED wiring  # not connected
  Due = Arduino Due / interface
  U2 = U2 / SN74LVC245AN / 3.3 V
  HDMI_switch = HDMI switch / modification taps
  Silver_button = Silver arcade button
  C2_100_nF = Capacitor
  R5_100_kohm = Resistor
  HDMI_notes = Manual switching and input routing  # not connected

nets:
  N1: JA.JA4_/_AB18_/_LED_data, U1.2_A1_/_LED_data_IN, R4_10_kohm.1
  GND: JA.JA5_/_GND, JA.JA11_/_GND, LED_power.GND, U1.3_A2_/_GND, U1.4_A3_/_GND, U1.5_A4_/_GND, U1.6_A5_/_GND, U1.7_A6_/_GND, U1.8_A7_/_GND, U1.9_A8_/_GND, U1.10_GND, U1.19_/OE_/_GND, LED1.GND, LED2.GND, LED3.GND, LED4_optional.GND, C1_100_nF.-_/_GND, C3_1000_uF_10_V.-_/_GND, R4_10_kohm.2, Due.GND, U2.3_A2_/_GND, U2.4_A3_/_GND, U2.5_A4_/_GND, U2.6_A5_/_GND, U2.7_A6_/_GND, U2.8_A7_/_GND, U2.9_A8_/_GND, U2.10_GND, U2.19_/OE_/_GND, HDMI_switch.GND_/_switch_logic_return, Silver_button.COM_/_switch_ground, C2_100_nF.-_/_GND, R5_100_kohm.1
  N2: LED_power.+5_V_LED, U1.1_DIR_/_tie_+5_V, U1.20_VCC_/_+5_V_LED, LED1.+5_V, LED2.+5_V, LED3.+5_V, LED4_optional.+5_V, C1_100_nF.+_/_rail, C3_1000_uF_10_V.+_/_rail
  N3: U1.18_B1_/_5_V_data_OUT, R1_330_ohm.1
  N4: R1_330_ohm.2, LED1.DIN
  N5: LED1.DOUT, LED2.DIN
  N6: LED2.DOUT, LED3.DIN
  N7: LED3.DOUT, LED4_optional.DIN
  N8: Due.3.3_V_for_U2_only, U2.1_DIR_/_tie_Due_3.3_V, U2.20_VCC_/_Due_3.3_V, C2_100_nF.+_/_rail
  N9: Due.D8_/_status_INPUT, U2.18_B1_/_3.3_V_OUT
  N10: U2.2_A1_/_status_5_V_IN, HDMI_switch.STATUS_5V_/_measured_logic, R5_100_kohm.2
  N11: HDMI_switch.TOGGLE_N_/_active_low, Silver_button.NO_/_normally_open

custom parts:
  Nexys Video / JA: Logical wiring symbol. Connector labels identify real board pins or complete cables. Not a physical board footprint. PCB fabrication is not supported by this documentation part.
  Regulated LED supply: Logical wiring symbol. Connector labels identify real board pins or complete cables. Not a physical board footprint. PCB fabrication is not supported by this documentation part.
  U1 / SN74HCT245N / 5 V: Logical wiring symbol. Connector labels identify real board pins or complete cables. Not a physical board footprint. PCB fabrication is not supported by this documentation part.
  Resistor: Logical wiring symbol. Connector labels identify real board pins or complete cables. Not a physical board footprint. PCB fabrication is not supported by this documentation part.
  SK6812 RGB pixel: Logical wiring symbol. Connector labels identify real board pins or complete cables. Not a physical board footprint. PCB fabrication is not supported by this documentation part.
  Capacitor: Logical wiring symbol. Connector labels identify real board pins or complete cables. Not a physical board footprint. PCB fabrication is not supported by this documentation part.
  Capacitor: Logical wiring symbol. Connector labels identify real board pins or complete cables. Not a physical board footprint. PCB fabrication is not supported by this documentation part.
  LED wiring: Logical wiring symbol. Connector labels identify real board pins or complete cables. Not a physical board footprint. PCB fabrication is not supported by this documentation part.
  Arduino Due / interface: Logical wiring symbol. Connector labels identify real board pins or complete cables. Not a physical board footprint. PCB fabrication is not supported by this documentation part.
  U2 / SN74LVC245AN / 3.3 V: Logical wiring symbol. Connector labels identify real board pins or complete cables. Not a physical board footprint. PCB fabrication is not supported by this documentation part.
  HDMI switch / modification taps: Logical wiring symbol. Connector labels identify real board pins or complete cables. Not a physical board footprint. PCB fabrication is not supported by this documentation part.
  Silver arcade button: Logical wiring symbol. Connector labels identify real board pins or complete cables. Not a physical board footprint. PCB fabrication is not supported by this documentation part.
  Manual switching and input routing: Logical wiring symbol. Connector labels identify real board pins or complete cables. Not a physical board footprint. PCB fabrication is not supported by this documentation part.
