# Fritzing sketch 04-realistic-breadboard (saved by Fritzing 1.0.1)

parts:
  Monitor = Monitor
  Pi = Raspberry Pi - USB and HDMI
  HDMI_switch = HDMI switch - illustrative
  FPGA = Nexys Video - illustrated
  Speakers = Powered speakers
  Due = Arduino Due - physical wiring
  Interface = LED and status interface assembly
  Trackball = Trackball - illustrative
  Pixels = SK6812 RGB strip - 3 or 4 pixels
  LED_power = LED 5 V supply
  Silver_button = Silver HDMI button
  P1_joystick = Arcade joystick
  P1_START = Arcade button
  P1_SELECT = Arcade button
  P1_A = Arcade button
  P1_B = Arcade button
  P2_joystick = Arcade joystick
  P2_START = Arcade button
  P2_SELECT = Arcade button
  P2_A = Arcade button
  P2_B = Arcade button
  Physical_view_notes = Physical view notes  # not connected

nets:
  N1: Monitor.HDMI, HDMI_switch.HDMI_out
  N2: Pi.USB_host_/_Due, Due.Native_USB
  N3: Pi.USB_host_/_JTAG, FPGA.PROG
  N4: Pi.HDMI, HDMI_switch.HDMI_1
  N5: HDMI_switch.HDMI_2, FPGA.HDMI_OUT
  N6: HDMI_switch.STATUS_5V, Interface.SW_STATUS
  N7: HDMI_switch.Button_NO, Silver_button.NO
  GND: HDMI_switch.Switch_GND, FPGA.JA5, FPGA.JA11, Due.gnd2, Interface.GND, Interface.LED_GND, Interface.SW_GND, Pixels.GND, LED_power.GND, Silver_button.COM, P1_joystick.COM, P1_START.COM, P1_SELECT.COM, P1_A.COM, P1_B.COM, P2_joystick.COM, P2_START.COM, P2_SELECT.COM, P2_A.COM, P2_B.COM
  N8: FPGA.JA6, Interface.JA6_3V3
  N9: FPGA.JA4, Interface.JA4_LED
  N10: FPGA.JA3, Due.D4, Interface.JA3_DATA1
  N11: FPGA.JA2, Due.D3
  N12: FPGA.JA1, Due.D2
  N13: FPGA.JA9, Due.D7, Interface.JA9_DATA2
  N14: FPGA.JA8, Due.D6
  N15: FPGA.JA7, Due.D5
  N16: FPGA.LINE_OUT, Speakers.3.5mm_stereo
  N17: FPGA.USB_HOST, Trackball.USB_mouse_cable
  N18: Due.3v3, Interface.Due_3V3
  N19: Due.D8, Interface.D8_status
  N20: Due.D22, P1_A.NO
  N21: Due.D23, P1_B.NO
  N22: Due.D24, P1_SELECT.NO
  N23: Due.D25, P1_START.NO
  N24: Due.D26, P1_joystick.UP
  N25: Due.D27, P1_joystick.DOWN
  N26: Due.D28, P1_joystick.LEFT
  N27: Due.D29, P1_joystick.RIGHT
  N28: Due.D30, P2_A.NO
  N29: Due.D31, P2_B.NO
  N30: Due.D32, P2_SELECT.NO
  N31: Due.D33, P2_START.NO
  N32: Due.D34, P2_joystick.UP
  N33: Due.D35, P2_joystick.DOWN
  N34: Due.D36, P2_joystick.LEFT
  N35: Due.D37, P2_joystick.RIGHT
  N36: Interface.LED_DIN, Pixels.DIN
  N37: Interface.LED_+5V, Interface.5V_IN, Pixels.+5_V, LED_power.5_V

custom parts:
  Monitor: Logical wiring symbol. Connector labels identify real board pins or complete cables. Not a physical board footprint. PCB fabrication is not supported by this documentation part.
  Raspberry Pi - USB and HDMI: Logical wiring symbol. Connector labels identify real board pins or complete cables. Not a physical board footprint. PCB fabrication is not supported by this documentation part.
  HDMI switch - illustrative: Logical wiring symbol. Connector labels identify real board pins or complete cables. Not a physical board footprint. PCB fabrication is not supported by this documentation part.
  Nexys Video - illustrated: Logical wiring symbol. Connector labels identify real board pins or complete cables. Not a physical board footprint. PCB fabrication is not supported by this documentation part.
  Powered speakers: Logical wiring symbol. Connector labels identify real board pins or complete cables. Not a physical board footprint. PCB fabrication is not supported by this documentation part.
  Arduino Due - physical wiring: Logical wiring symbol. Connector labels identify real board pins or complete cables. Not a physical board footprint. PCB fabrication is not supported by this documentation part.
  LED and status interface assembly: Logical wiring symbol. Connector labels identify real board pins or complete cables. Not a physical board footprint. PCB fabrication is not supported by this documentation part.
  Trackball - illustrative: Logical wiring symbol. Connector labels identify real board pins or complete cables. Not a physical board footprint. PCB fabrication is not supported by this documentation part.
  SK6812 RGB strip - 3 or 4 pixels: Logical wiring symbol. Connector labels identify real board pins or complete cables. Not a physical board footprint. PCB fabrication is not supported by this documentation part.
  LED 5 V supply: Logical wiring symbol. Connector labels identify real board pins or complete cables. Not a physical board footprint. PCB fabrication is not supported by this documentation part.
  Silver HDMI button: Logical wiring symbol. Connector labels identify real board pins or complete cables. Not a physical board footprint. PCB fabrication is not supported by this documentation part.
  Arcade joystick: Logical wiring symbol. Connector labels identify real board pins or complete cables. Not a physical board footprint. PCB fabrication is not supported by this documentation part.
  Arcade button: Logical wiring symbol. Connector labels identify real board pins or complete cables. Not a physical board footprint. PCB fabrication is not supported by this documentation part.
  Arcade button: Logical wiring symbol. Connector labels identify real board pins or complete cables. Not a physical board footprint. PCB fabrication is not supported by this documentation part.
  Arcade button: Logical wiring symbol. Connector labels identify real board pins or complete cables. Not a physical board footprint. PCB fabrication is not supported by this documentation part.
  Physical view notes: Logical wiring symbol. Connector labels identify real board pins or complete cables. Not a physical board footprint. PCB fabrication is not supported by this documentation part.
